# Fritzing sketch led-button (saved by Fritzing 0.9.2b)

parts:
  J1 = Raspberry Pi Header 40pin [form="♂ (male)" package=THT]
  S1 = Round Pushbutton
  S2 = Pushbutton [package=THT]
  R1 = Resistor [tolerance=±5% resistance=220 package="0402 [SMD]"]

nets:
  N1: J1.GIPO5, S1.leg0
  N2: J1.GND, S2.leg0
  N3: J1.GIPO25, S2.leg1
  N4: S1.leg1, R1.Pin_0

custom parts:
  Raspberry Pi Header 40pin: Raspberry Pi 40 pin header - for creating your own shields.
