# Fritzing sketch wiring (saved by Fritzing 0.9.2b)
stripboards: 1

parts:
  S1 = Round Pushbutton
  S2 = Pushbutton [package=THT]
  S3 = Round Pushbutton
  S4 = Pushbutton [package=THT]
  S5 = Round Pushbutton
  S6 = Pushbutton [package=THT]
  S7 = Round Pushbutton
  S8 = Pushbutton [package=THT]
  Part1 = Adafruit Stereo 3W Speaker Bonnet [part_number="Adafruit #"]
  R1 = Resistor [tolerance=±5% resistance=220 package=THT]

nets:
  N1: S1.leg0, Part1.GPIO5
  N2: S1.leg1, S2.leg0, S3.leg1, S4.leg0
  N3: S2.leg1, Part1.GPIO25
  N4: S3.leg0, Part1.GPIO24
  N5: S4.leg1, Part1.GPIO23
  N6: S5.leg0, Part1.GPIO22
  N7: S5.leg1, S6.leg0, S7.leg1, S8.leg0
  N8: S6.leg1, Part1.GPIO27
  N9: S7.leg0, Part1.GPIO17
  N10: S8.leg1, Part1.GPIO4
  N11: Part1.GND, R1.Pin_1

custom parts:
  Adafruit Stereo 3W Speaker Bonnet: Hey Mr. DJ! Turn up that Raspberry Pi mix to the max with this cute 3W Stereo Amplifier Bonnet for Raspberry Pi. (It's not big enough to be an official HAT, so we called it a bonnet, you see?) It's the exact same size as a Raspberry Pi Zero but works with any and all Raspberry Pi computers with a 2x20 connector - A+, B+, Zero, Pi 2, Pi 3, etc. This Bonnet uses I2S a digital sound standard, so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
